# Fritzing sketch supurgerobot (saved by Fritzing 0.9.1b)
circuit board: 14.8622cm x 5.65968cm
breadboards: 1

parts:
  U1 = Voltage Regulator - 5V [package="TO220 [THT]"]
  C1 = Electrolytic Capacitor [capacitance=100nF package="100 mil [THT, electrolytic]"]
  C2 = Electrolytic Capacitor [capacitance=100nF package="100 mil [THT, electrolytic]"]
  S1 = Toggle Switch [package=THT]
  J1 = Screw terminal - 2 pins [package=THT]
  C3 = Ceramic Capacitor [capacitance=1nF package="200 mil [THT, multilayer]"]
  U2 = L298 [package=multiwatt15]
  MOTOR_SOL = Header 2 [package=screwterminal-3.5mm-2_lock]
  MOTOR_SAG = Header 2 [package=screwterminal-3.5mm-2_lock]
  D8 = Rectifier Diode [part_number=1N4001 package="300 mil [THT]"]
  D1 = Rectifier Diode [part_number=1N4001 package="300 mil [THT]"]
  D2 = Rectifier Diode [part_number=1N4001 package="300 mil [THT]"]
  D3 = Rectifier Diode [part_number=1N4001 package="300 mil [THT]"]
  D4 = Rectifier Diode [part_number=1N4001 package="300 mil [THT]"]
  D5 = Rectifier Diode [part_number=1N4001 package="300 mil [THT]"]
  D7 = Rectifier Diode [part_number=1N4001 package="300 mil [THT]"]
  D6 = Rectifier Diode [part_number=1N4001 package="300 mil [THT]"]
  R1 = Resistor [tolerance=±5% resistance=220 package=THT]
  LED2 = LED - 5mm [color="Red (633nm)" package="5 mm [THT]"]
  J2 = minik bord sol Generic female header - 20 pins [form="♀ (female)" package=THT]
  J3 = minik bord SAĞ Generic female header - 20 pins [form="♀ (female)" package=THT]

nets:
  VMOT: U1.input_voltage, C1.+, S1.COM, U2.VS, D1.cathode, D2.cathode, D3.cathode, D4.cathode
  GND: U1.GND_TOPRAK, C1.-, C2.-, J1.pin2, C3.0, U2.CSA, U2.GND, U2.CSB, D8.anode, D5.anode, D7.anode, D6.anode, LED2.cathode, J2.G, J3.G
  5V: U1.output_voltage, C2.+, C3.1, U2.VLS, R1.Pin_0, J2.5V
  N1: S1.L2, J1.pin1
  N2: U2.OUT1, MOTOR_SOL.1, D1.anode, D6.cathode
  N3: U2.OUT2, MOTOR_SOL.2, D2.anode, D7.cathode
  MOTOR_SOL_1: U2.IN1, J3.B1
  MOTOR_SOL_PWM: U2.ENA, J3.A0
  MOTOR_SOL_2: U2.IN2
  MOTOR_SAG_1: U2.IN3, J3.B10
  MOTOR_SAG_PWM: U2.ENB, J3.A1
  MOTOR_SAG_2: U2.IN4, J3.B11
  N4: U2.OUT3, MOTOR_SAG.1, D8.cathode, D3.anode
  N5: U2.OUT4, MOTOR_SAG.2, D4.anode, D5.cathode
  N6: R1.Pin_1, LED2.anode
  SOL_BIYIK: J2.B12
  SAG_BIYIK: J2.B13
  BUZZER: J2.B14
  VAKUM: J2.A9
  ON_SENSOR: J3.A2

custom parts:
  Voltage Regulator - 5V: 5V DC Voltage Regulator
  minik bord sol Generic female header - 20 pins: Generic female header minik bord sol
  minik bord SAĞ Generic female header - 20 pins: Generic female header minik bord SAĞ
